// Logisim project ampel.circ as structural Verilog: 6 circuits, main circuit main
module main (
  input  Ft
);

  wire as_1_ag, as_1_ar, as_1_ay, as_1_fg, as_1_fr, clock_1_out, d_ff_1_q, d_ff_2_q, d_ff_3_q, d_ff_4_q,
       tdelay_1_d, \tgrün_1_tg , tsperr_1_ts, \üs_1_z0plus , \üs_1_z1plus , \üs_1_z2plus ;

  Clock clock_1 (.out(clock_1_out));
  D_Flip_Flop d_ff_1 (.clk(clock_1_out), .D(Ft), .Q(d_ff_1_q));  // open: Qn, preset, en, reset
  \üs  \u_üs_1  (
    .Ft(d_ff_1_q), .D(tdelay_1_d), .tg(\tgrün_1_tg ), .ts(tsperr_1_ts), .Z2(d_ff_2_q), .Z1(d_ff_3_q),
    .Z0(d_ff_4_q), .Z2Plus(\üs_1_z2plus ), .Z1Plus(\üs_1_z1plus ), .Z0Plus(\üs_1_z0plus ));
  D_Flip_Flop d_ff_2 (.clk(clock_1_out), .D(\üs_1_z2plus ), .Q(d_ff_2_q));  // open: Qn, preset, en, reset
  D_Flip_Flop d_ff_3 (.clk(clock_1_out), .D(\üs_1_z1plus ), .Q(d_ff_3_q));  // open: Qn, preset, en, reset
  D_Flip_Flop d_ff_4 (.clk(clock_1_out), .D(\üs_1_z0plus ), .Q(d_ff_4_q));  // open: Qn, preset, en, reset
  tDelay tdelay_1 (.takt(clock_1_out), .Fg(as_1_fg), .Ar(as_1_ar), .Ag(as_1_ay), .d(tdelay_1_d));
  tSperr tsperr_1 (.takt(clock_1_out), .Fg(as_1_fg), .ts(tsperr_1_ts));
  \tGrün  \tgrün_1  (.takt(clock_1_out), .Fg(as_1_fg), .Fr(as_1_fr), .tg(\tgrün_1_tg ));
  as as_1 (
    .z0(d_ff_4_q), .Z1(d_ff_3_q), .z2(d_ff_2_q), .Fr(as_1_fr), .Fg(as_1_fg), .Ar(as_1_ar), .Ay(as_1_ay),
    .Ag(as_1_ag));
  LED led_1 (.in(as_1_fr));
  LED led_2 (.in(as_1_fg));
  LED led_3 (.in(as_1_ar));
  LED led_4 (.in(as_1_ay));
  LED led_5 (.in(as_1_ag));
endmodule

module \üs  (
  input  Ft,
  input  D,
  input  tg,
  input  ts,
  input  Z2,
  input  Z1,
  input  Z0,
  output Z2Plus,
  output Z1Plus,
  output Z0Plus
);

  wire and_1_out, and_2_out, and_3_out, and_4_out, and_5_out, and_6_out, and_7_out, and_8_out, and_9_out,
       and_10_out, and_11_out, and_12_out, and_13_out, and_14_out, and_15_out, and_16_out, and_17_out,
       and_18_out, and_19_out, and_20_out, and_21_out, and_22_out, and_23_out, and_24_out, and_25_out,
       and_26_out, and_27_out, and_28_out, and_29_out, and_30_out, and_31_out, not_1_out, not_2_out,
       not_3_out, not_4_out, not_5_out, not_6_out, not_7_out, not_8_out, not_9_out, not_10_out, not_11_out,
       not_12_out, not_13_out, not_14_out, not_15_out, not_16_out, not_17_out, not_18_out, not_19_out,
       not_20_out, not_21_out, not_22_out, not_23_out, not_24_out, not_25_out, not_26_out, not_27_out,
       not_28_out, not_29_out, not_30_out, not_31_out, not_32_out, not_33_out, not_34_out, not_35_out,
       not_36_out, not_37_out, not_38_out, not_39_out, not_40_out, not_41_out, not_42_out, not_43_out,
       not_44_out, not_45_out, not_46_out, not_47_out, not_48_out, not_49_out, not_50_out, not_51_out,
       not_52_out, not_53_out, not_54_out, not_55_out, not_56_out, not_57_out, not_58_out, not_59_out,
       not_60_out, not_61_out, not_62_out, not_63_out;

  not not_1 (not_1_out, tg);
  not not_2 (not_2_out, Z2);
  not not_3 (not_3_out, Z0);
  not not_4 (not_4_out, Z1);
  not not_5 (not_5_out, Z0);
  not not_6 (not_6_out, Z1);
  not not_7 (not_7_out, D);
  not not_8 (not_8_out, Ft);
  not not_9 (not_9_out, Z0);
  not not_10 (not_10_out, Z1);
  not not_11 (not_11_out, D);
  not not_12 (not_12_out, Z1);
  not not_13 (not_13_out, Z0);
  not not_14 (not_14_out, Z1);
  not not_15 (not_15_out, Z2);
  not not_16 (not_16_out, ts);
  not not_17 (not_17_out, Z1);
  not not_18 (not_18_out, Z2);
  not not_19 (not_19_out, Z0);
  not not_20 (not_20_out, Z2);
  not not_21 (not_21_out, D);
  not not_22 (not_22_out, Z2);
  not not_23 (not_23_out, Z0);
  not not_24 (not_24_out, Z1);
  not not_25 (not_25_out, D);
  not not_26 (not_26_out, Ft);
  not not_27 (not_27_out, Z1);
  not not_28 (not_28_out, Z1);
  not not_29 (not_29_out, D);
  not not_30 (not_30_out, Z0);
  not not_31 (not_31_out, D);
  not not_32 (not_32_out, ts);
  not not_33 (not_33_out, Z0);
  not not_34 (not_34_out, Z1);
  not not_35 (not_35_out, Z2);
  not not_36 (not_36_out, Z2);
  not not_37 (not_37_out, Z1);
  not not_38 (not_38_out, Z0);
  not not_39 (not_39_out, Z2);
  not not_40 (not_40_out, Z1);
  not not_41 (not_41_out, Z0);
  and and_1 (and_1_out, not_1_out, not_2_out, Z1, Z0);
  and and_2 (and_2_out, not_3_out, not_4_out, Z2, D);
  and and_3 (and_3_out, not_5_out, not_6_out, not_7_out, Z2, not_8_out);
  and and_4 (and_4_out, not_9_out, not_10_out, Z2, not_11_out, Ft);
  and and_5 (and_5_out, not_12_out, Z0, Z2, D);
  not not_42 (not_42_out, Z1);
  not not_43 (not_43_out, D);
  and and_6 (and_6_out, not_42_out, Z0, not_43_out, Z2, Ft);
  not not_44 (not_44_out, Z0);
  and and_7 (and_7_out, not_44_out, Z1, Z2, D);
  not not_45 (not_45_out, Z0);
  and and_8 (and_8_out, not_45_out, Z1, not_46_out, Z2);
  not not_46 (not_46_out, D);
  and and_9 (and_9_out, Z0, Z1, Z2, ts);
  not not_47 (not_47_out, D);
  and and_10 (and_10_out, not_47_out, not_48_out, Z0, not_49_out);
  not not_48 (not_48_out, Z2);
  not not_49 (not_49_out, Z1);
  not not_50 (not_50_out, Z0);
  and and_11 (and_11_out, not_50_out, Z1, not_51_out, D);
  not not_51 (not_51_out, Z2);
  not not_52 (not_52_out, Z0);
  and and_12 (and_12_out, not_52_out, Z1, not_53_out, not_54_out);
  not not_53 (not_53_out, Z2);
  not not_54 (not_54_out, D);
  not not_55 (not_55_out, Z2);
  and and_13 (and_13_out, not_55_out, Z0, Z1, tg);
  not not_56 (not_56_out, Z0);
  and and_14 (and_14_out, not_56_out, Z2, not_57_out, Ft, not_58_out);
  not not_57 (not_57_out, Z1);
  not not_58 (not_58_out, D);
  not not_59 (not_59_out, Z1);
  not not_60 (not_60_out, D);
  and and_15 (and_15_out, not_59_out, Z0, not_60_out, Z2, Ft);
  not not_61 (not_61_out, Z0);
  and and_16 (and_16_out, not_61_out, Z1, Z2, D);
  not not_62 (not_62_out, Z0);
  and and_17 (and_17_out, not_62_out, Z1, not_63_out, Z2);
  not not_63 (not_63_out, D);
  and and_18 (and_18_out, Z0, Z1, Z2, ts);
  and and_19 (and_19_out, not_13_out, not_14_out, Ft, not_15_out, not_16_out);
  and and_20 (and_20_out, Z0, not_17_out, not_18_out, D);
  and and_21 (and_21_out, not_19_out, not_20_out, Z1, not_21_out);
  and and_22 (and_22_out, not_22_out, Z0, Z1, tg);
  and and_23 (and_23_out, not_23_out, not_24_out, Z2, not_25_out, not_26_out);
  and and_24 (and_24_out, not_27_out, Z0, Z2, D);
  and and_25 (and_25_out, not_28_out, Z0, not_29_out, Z2, Ft);
  and and_26 (and_26_out, not_30_out, Z1, not_31_out, Z2);
  and and_27 (and_27_out, Z0, Z1, Z2, ts);
  and and_28 (and_28_out, Z0, not_32_out, Z1, Z2);
  and and_29 (and_29_out, not_33_out, ts, not_34_out, Ft, not_35_out);
  and and_30 (and_30_out, not_36_out, Ft, not_37_out, ts, not_38_out);
  and and_31 (and_31_out, not_39_out, Ft, not_40_out, ts, not_41_out);
  or or_1 (Z1Plus, and_14_out, and_10_out, and_11_out, and_12_out, and_13_out, and_15_out, and_16_out, and_17_out, and_18_out, and_30_out);
  or or_2 (Z2Plus, and_5_out, and_1_out, and_2_out, and_3_out, and_4_out, and_6_out, and_7_out, and_8_out, and_9_out, and_31_out);
  or or_3 (Z0Plus, and_19_out, and_20_out, and_21_out, and_22_out, and_23_out, and_29_out, and_24_out, and_25_out, and_26_out, and_27_out, and_28_out);
endmodule

module as (
  input  z0,
  input  Z1,
  input  z2,
  output Fr,
  output Fg,
  output Ar,
  output Ay,
  output Ag
);

  wire and_2_out, and_3_out, and_4_out, and_5_out, and_6_out, and_7_out, and_8_out, not_1_out, not_2_out,
       not_3_out, not_4_out, not_5_out, not_6_out, not_7_out, not_8_out, not_9_out, not_10_out, not_11_out;

  not not_1 (not_1_out, Z1);
  not not_2 (not_2_out, z0);
  not not_3 (not_3_out, z2);
  not not_4 (not_4_out, z0);
  not not_5 (not_5_out, Z1);
  not not_6 (not_6_out, z2);
  not not_7 (not_7_out, Z1);
  not not_8 (not_8_out, z0);
  not not_9 (not_9_out, z0);
  not not_10 (not_10_out, Z1);
  not not_11 (not_11_out, z2);
  or or_1 (Fr, not_1_out, z2, not_2_out);
  and and_1 (Fg, not_3_out, Z1, z0);
  and and_2 (and_2_out, Z1, not_4_out);
  and and_3 (and_3_out, not_5_out, z2);
  and and_4 (and_4_out, not_6_out, Z1, z0);
  and and_5 (and_5_out, not_7_out, z0);
  and and_6 (and_6_out, not_8_out, z2, Z1);
  and and_7 (and_7_out, not_9_out, not_10_out, not_11_out);
  and and_8 (and_8_out, z0, Z1, z2);
  or or_2 (Ar, and_2_out, and_3_out, and_4_out);
  or or_3 (Ay, and_5_out, and_6_out);
  or or_4 (Ag, and_7_out, and_8_out);
endmodule

module tDelay (
  input  takt,
  input  Fg,
  input  Ar,
  input  Ag,
  output d
);

  wire and_1_out, counter_1_carry, counter_2_carry, or_1_out;

  and and_1 (and_1_out, Ar, Ag);
  Counter #(.width(12), .max('hfff)) counter_1 (
    .carry(counter_1_carry), .clk(takt), .clr(Fg));  // open: load, D, count, Q
  Counter #(.width(10), .max('h3ff)) counter_2 (
    .count(and_1_out), .carry(counter_2_carry), .clk(takt));  // open: load, D, Q, clr
  or or_1 (or_1_out, counter_1_carry, counter_2_carry);
  not not_1 (d, or_1_out);
endmodule

module \tGrün  (
  input  takt,
  input  Fg,
  input  Fr,
  output tg
);

  wire and_1_out, not_1_out, not_2_out, not_3_out, not_4_out, not_5_out, not_6_out, not_7_out, not_8_out,
       not_9_out, not_10_out;
  wire [14:0] counter_1_q;

  Counter #(.width(15), .max('h7fff)) counter_1 (
    .count(Fg), .Q(counter_1_q), .clk(takt), .clr(Fr));  // open: load, D, carry
  not not_1 (not_1_out, counter_1_q[0]);
  not not_2 (not_2_out, counter_1_q[1]);
  not not_3 (not_3_out, counter_1_q[2]);
  not not_4 (not_4_out, counter_1_q[4]);
  not not_5 (not_5_out, counter_1_q[6]);
  not not_6 (not_6_out, counter_1_q[8]);
  not not_7 (not_7_out, counter_1_q[12]);
  not not_8 (not_8_out, counter_1_q[3]);
  not not_9 (not_9_out, counter_1_q[7]);
  not not_10 (not_10_out, counter_1_q[13]);
  and and_1 (and_1_out, not_1_out, not_2_out, not_3_out, not_8_out, not_4_out, counter_1_q[5], not_5_out, not_9_out, not_6_out, counter_1_q[9], counter_1_q[10], counter_1_q[11], not_7_out, not_10_out, counter_1_q[14]);
  not not_11 (tg, and_1_out);
endmodule

module tSperr (
  input  takt,
  input  Fg,
  output ts
);

  wire counter_1_carry;

  Counter #(.width(15), .max('h7fff)) counter_1 (
    .count(ts), .carry(counter_1_carry), .clk(takt), .clr(Fg));  // open: load, D, Q
  not not_1 (ts, counter_1_carry);
endmodule
